// Digital circuit CORDICcircuit_draft.dig as structural Verilog
module CORDICcircuit_draft (
  input  [8:0] z_input,
  input  Processing,
  input  clk,
  input  Enable_reg_z,
  input  Enable_reg_y,
  input  Enable_reg_x,
  input  Iteration_n
);

  wire comparator_1_gt, not_1_out;
  wire [8:0] add_3_s, lookuptable_1_out, multiplexer_1_out, multiplexer_4_out, Register_z_q, sub_3_s;
  wire [9:0] add_1_s, add_2_s, multiplexer_2_out, multiplexer_3_out, multiplexer_5_out, multiplexer_6_out,
       Register_x_q, Register_y_q, sub_1_s, sub_2_s, x_shifter_out, y_shifter_out;

  LookUpTable #(.Bits(9)) lookuptable_1 (
    .in0(Iteration_n), .in1(Iteration_n), .in2(Iteration_n), .in3(Iteration_n), .in4(Iteration_n),
    .in5(Iteration_n), .in6(Iteration_n), .in7(Iteration_n), .in8(Iteration_n), .in9(Iteration_n),
    .out(lookuptable_1_out));
  Multiplexer #(.Bits(9)) multiplexer_1 (
    .sel(not_1_out), .in_0(multiplexer_4_out), .in_1(z_input), .out(multiplexer_1_out));
  Sub #(.Bits(10)) sub_1 (.a(Register_y_q), .b(x_shifter_out), .c_i(1'b0), .s(sub_1_s));  // open: c_o
  Add #(.Bits(10)) add_1 (.a(Register_y_q), .b(x_shifter_out), .c_i(1'b0), .s(add_1_s));  // open: c_o
  Add #(.Bits(10)) add_2 (.a(Register_x_q), .b(y_shifter_out), .c_i(1'b0), .s(add_2_s));  // open: c_o
  Sub #(.Bits(10)) sub_2 (.a(Register_x_q), .b(y_shifter_out), .c_i(1'b0), .s(sub_2_s));  // open: c_o
  Register #(.Bits(9)) Register_z (.D(multiplexer_1_out), .C(clk), .en(Enable_reg_z), .Q(Register_z_q));
  Add #(.Bits(9)) add_3 (.a(Register_z_q), .b(lookuptable_1_out), .c_i(1'b0), .s(add_3_s));  // open: c_o
  Sub #(.Bits(9)) sub_3 (.a(Register_z_q), .b(lookuptable_1_out), .c_i(1'b0), .s(sub_3_s));  // open: c_o
  Multiplexer #(.Bits(10)) multiplexer_2 (
    .sel(comparator_1_gt), .in_0(sub_1_s), .in_1(add_1_s), .out(multiplexer_2_out));
  Multiplexer #(.Bits(10)) multiplexer_3 (
    .sel(comparator_1_gt), .in_0(add_2_s), .in_1(sub_2_s), .out(multiplexer_3_out));
  Comparator #(.Bits(9)) comparator_1 (.a(Register_z_q), .b({9{1'b0}}), .gt(comparator_1_gt));  // open: eq, lt
  Multiplexer #(.Bits(9)) multiplexer_4 (
    .sel(comparator_1_gt), .in_0(add_3_s), .in_1(sub_3_s), .out(multiplexer_4_out));
  not not_1 (not_1_out, Processing);
  Multiplexer #(.Bits(10)) multiplexer_5 (
    .sel(not_1_out), .in_0(multiplexer_2_out), .in_1({10{1'b0}}), .out(multiplexer_5_out));
  Multiplexer #(.Bits(10)) multiplexer_6 (
    .sel(not_1_out), .in_0(multiplexer_3_out), .in_1(10'h1), .out(multiplexer_6_out));
  Register #(.Bits(10)) Register_y (.D(multiplexer_5_out), .C(clk), .en(Enable_reg_y), .Q(Register_y_q));
  Register #(.Bits(10)) Register_x (.D(multiplexer_6_out), .C(clk), .en(Enable_reg_x), .Q(Register_x_q));
  BarrelShifter #(.Bits(10), .barrelSigned("true"), .direction("right")) y_shifter (
    .in(Register_y_q), .shift({5{1'b0}}), .out(y_shifter_out));
  BarrelShifter #(.Bits(10), .barrelSigned("true"), .direction("right")) x_shifter (
    .in(Register_x_q), .shift({5{1'b0}}), .out(x_shifter_out));
endmodule
